# Fritzing sketch esp32_circuit (saved by Fritzing 0.9.5d)
breadboards: 1

parts:
  M1 = DOIT Esp32 DevKit v1 (30 pins long, 11 pins width) [part_number=ESP32S-PIN30]
  DHT11_1 = DHT11 module
  Mod1 = KY-016 RGB Full Color LED Module [package="Breakout board"]

nets:
  3V3: M1.3V3, DHT11_1.VCC
  GND: M1.GND, DHT11_1.GND, Mod1.-
  N1: M1.D15, DHT11_1.DATA
  N2: M1.D14, Mod1.B
  N3: M1.D12, Mod1.G
  N4: M1.D13, Mod1.R

custom parts:
  DOIT Esp32 DevKit v1 (30 pins long, 11 pins width): The DOIT Esp32 DevKit v1 is one of the development board created by DOIT to evaluate the ESP-WROOM-32 module. It is based on the ESP32 microcontroller that boasts Wifi, Bluetooth, Ethernet and Low Power support all in a single chip. (vanepp) made breadboard work, adjusted pin numbering and labels and reduced size of schematic and cleaned up pcb. This chip is 30pins long (2 x15) and 11 pins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
  DHT11 module: https://cdn-learn.adafruit.com/downloads/pdf/dht.pdf DHT11 black pcb module reference by:https://github.com/adafruit/Fritzing-Library/blob/master/parts/DHT11%20Humitidy%20and%20Temperature%20Sensor.fzpz
  KY-016 RGB Full Color LED Module: KY-016 Arduino full color 5mm RGB LED, different colors can be obtained by mixing the three primary colors.
